// Logisim project seq_circuit.circ as structural Verilog: 1 circuit, main circuit main
module main (
  input  x,
  input  y,
  output Q,
  output S
);

  wire and_1_out, and_2_out, and_3_out, Clock_out, or_1_out, xor_1_out;

  and and_1 (and_1_out, x, Q);
  and and_2 (and_2_out, y, Q);
  and and_3 (and_3_out, x, y);
  xor xor_1 (xor_1_out, x, y);
  or or_1 (or_1_out, and_1_out, and_2_out, and_3_out);
  xor xor_2 (S, Q, xor_1_out);
  Clock Clock (.out(Clock_out));
  D_Flip_Flop d_ff_1 (.clk(Clock_out), .D(or_1_out), .Q(Q));  // open: Qn, preset, en, reset
endmodule
